# Fritzing sketch piezo_led_photoresistor (saved by Fritzing 0.3.19b)
breadboards: 1

parts:
  Arduino1 = Arduino
  J1 = Piezo Speaker
  R1 = Photocell (LDR) [package=THT]
  R2 = Resistor [resistance=220 package=THT]
  LED1 = RGB LED (6 legs) [package="5 mm [THT]"]  # not connected

nets:
  N1: Arduino1.GND, J1.pin1, R2.Pin_1
  N2: Arduino1.D3, J1.pin2
  N3: Arduino1.+5V, R1.pin_0
  N4: Arduino1.A0, R1.pin_1, R2.Pin_0
