# Fritzing sketch randomlights (saved by Fritzing 0.3.19b)
breadboards: 1

parts:
  Arduino1 = Arduino
  R1 = Resistor [resistance=330 package=THT]
  LED1 = green LED - 5mm
  R1_2 = Resistor [resistance=330 package=THT]
  LED2 = Blue LED - 5mm
  LED3 = Red LED - 5mm
  R1_3 = Resistor [resistance=330 package=THT]
  R1_4 = Resistor [resistance=330 package=THT]
  LED4 = yellow LED - 5mm

nets:
  N1: Arduino1.GND, LED1.cathode, LED2.cathode, LED3.cathode, LED4.cathode
  N2: Arduino1.D7, R1.Pin_1
  N3: Arduino1.D6, R1_2.Pin_1
  N4: Arduino1.D5, R1_3.Pin_1
  N5: Arduino1.D4, R1_4.Pin_1
  N6: R1.Pin_0, LED1.anode
  N7: R1_2.Pin_0, LED2.anode
  N8: LED3.anode, R1_3.Pin_0
  N9: R1_4.Pin_0, LED4.anode
